// Logisim project LogismProjects.circ as structural Verilog: 4 circuits, main circuit main
module main (
  input  LOAD,
  input  Q,
  input  BIT,
  output D
);

  wire and_1_out, and_2_out, not_1_out;

  not not_1 (not_1_out, LOAD);
  and and_1 (and_1_out, not_1_out, Q);
  and and_2 (and_2_out, LOAD, BIT);
  or or_1 (D, and_1_out, and_2_out);
endmodule

module DigitalSPDTSwitch (
  input  S,
  input  A,
  input  B,
  output O
);

  wire and_1_out, and_2_out, and_3_out, and_4_out, and_5_out, and_6_out, and_7_out, and_8_out, not_1_out,
       not_2_out, not_3_out, not_4_out, or_1_out, or_2_out;

  not not_1 (not_1_out, S);
  not not_2 (not_2_out, S);
  not not_3 (not_3_out, A);
  and and_1 (and_1_out, not_1_out, A);
  not not_4 (not_4_out, B);
  and and_2 (and_2_out, not_2_out, A);
  and and_3 (and_3_out, S, not_3_out);
  and and_4 (and_4_out, S, A);
  and and_5 (and_5_out, and_1_out, not_4_out);
  and and_6 (and_6_out, and_2_out, B);
  and and_7 (and_7_out, and_3_out, B);
  and and_8 (and_8_out, and_4_out, B);
  or or_1 (or_1_out, and_5_out, and_6_out);
  or or_2 (or_2_out, and_7_out, and_8_out);
  or or_3 (O, or_1_out, or_2_out);
endmodule

module DigitalSPDTSwitchSimplified (
  input  S,
  input  A,
  input  B,
  output O
);

  wire and_1_out, and_2_out, not_1_out;

  not not_1 (not_1_out, S);
  and and_1 (and_1_out, not_1_out, A);
  and and_2 (and_2_out, S, B);
  or or_1 (O, and_1_out, and_2_out);
endmodule

module RegisterFeedbacker (
  input  LOAD,
  input  Q,
  input  BIT,
  output D
);

  wire and_1_out, and_2_out, not_1_out;

  not not_1 (not_1_out, LOAD);
  and and_1 (and_1_out, not_1_out, Q);
  and and_2 (and_2_out, LOAD, BIT);
  or or_1 (D, and_1_out, and_2_out);
endmodule
